# Fritzing sketch Tiny_Motor_Slave (saved by Fritzing 0.9.1b)
circuit board: 3.56299cm x 2.77625cm
perfboards: 1

parts:
  J1 = Screw terminal - 2 pins [package=THT]
  U1 = attiny85 [package=dip]
  LED1 = LED - 5mm [color="Red (633nm)" package="5 mm [THT]"]
  J2 = Screw terminal - 2 pins [package=THT]
  U2 = Voltage Regulator [package=to220-igo]
  J3 = Screw terminal - 2 pins [package=THT]
  J4 = Screw terminal - 2 pins [package=THT]
  R1 = Resistor [tolerance=±5% resistance=220 package=THT]

nets:
  N1: J1.pin1, U1.Pin_7
  N2: J1.pin2, U1.Pin_5
  N3: U1.Pin_2, J2.pin2
  N4: U1.Pin_3, J2.pin1
  N5: U1.Pin_4, LED1.cathode, U2.GND, J3.pin2, J4.pin1
  N6: U1.Pin_6, R1.Pin_1
  N7: U1.Pin_8, U2.OUT
  N8: LED1.anode, R1.Pin_0
  N9: U2.IN, J3.pin1, J4.pin2

notes:
  Power out to stepper driver along with step and direction (grey and yellow)
  power in 12/24VDC
  Orange - is SCL for i2c
  White - is SDA for i2c

// code stored in the sketch: Tiny_Motor_Slave.ino
#include <TinyWireS.h>

//this needs to change for each sensor
#define I2C_SLAVE_ADDR  0x01            // i2c slave address 

#define STEP_PIN      			4              // ATtiny Pin 3
#define DIR_PIN      				3              // ATtiny Pin 2
//#define LED							1              // ATtiny Pin 6
boolean direction, start;
uint16_t steps, speed;

// The default buffer size, Can't recall the scope of defines right now
#ifndef TWI_RX_BUFFER_SIZE
#define TWI_RX_BUFFER_SIZE ( 16 )
#endif

byte buffer[16];

void setup(){
  
  pinMode(STEP_PIN, OUTPUT);
  pinMode(DIR_PIN, OUTPUT);             
  pinMode(LED, INPUT);

  TinyWireS.begin(I2C_SLAVE_ADDR);      // init I2C Slave mode

  TinyWireS.onRecieve(recieveEvent);  //the function associated with a read request

	start = false;
}

//the i2c recieve handle which says how many bytes we are recieving
void recieveEvent(uint8_t howMany)
{  
	//Is it a clock sync or a data buffer
	if(howMnay>1){
		uint8_t count =0;
		while (TinyWireS.available()) { // loop through all 
			buffer[count++] = TinyWireS.receive(){  // receive byte
		}
	}
	else {
		start = true;
	}
}

void loop(){
  TinyWireS_stop_check(); //maybe it would be easier to attach this to a timer, will that cause issues with the callback?
}

//we should try to make this as non-blocking as possible
void step(){
	digitalWrite(STEP_PIN, HIGH); 
    delayMicroseconds(usDelay); 

    digitalWrite(STEP_PIN, LOW); 
}

//stop stepping
void stop(){

}
